// Logisim project hw_vga_sim.circ as structural Verilog: 7 circuits, main circuit main
module main (
  input  nRST
);

  wire CLK_out, HBeginPulse, HEndPulse, HSCAN_END, HVisEnd, sync_1_hsync_out, sync_1_hvis, sync_1_vis,
       sync_1_vsync_out, sync_1_vvis, VBeginPulse, VCOUNT_END, VEndPulse, VVisEnd;
  wire [11:0] HCOUNT_OUT, VCOUNT_OUT;

  Clock CLK (.out(CLK_out));
  HCount hcount_1 (
    .CLK(CLK_out), .nRST(nRST), .HCOUNT_OUT(HCOUNT_OUT), .BeginPulse(HBeginPulse), .EndPulse(HEndPulse),
    .HSCAN_END(HSCAN_END), .HVisEnd(HVisEnd));
  VCount vcount_1 (
    .CLK(CLK_out), .nRST(nRST), .HSCAN_END(HSCAN_END), .VCOUNT_OUT(VCOUNT_OUT), .VCOUNT_END(VCOUNT_END),
    .BeginPulse(VBeginPulse), .EndPulse(VEndPulse), .VVisEnd(VVisEnd));
  Sync sync_1 (
    .CLK(CLK_out), .nRST(nRST), .HBeginPulse(HBeginPulse), .HEndPulse(HEndPulse), .VBeginPulse(VBeginPulse),
    .VEndPulse(VEndPulse), .HCOUNT_END(HSCAN_END), .VCOUNT_END(VCOUNT_END), .HVisEnd(HVisEnd),
    .VVisEnd(VVisEnd), .HSYNC_OUT(sync_1_hsync_out), .VSYNC_OUT(sync_1_vsync_out), .HVis(sync_1_hvis),
    .VVis(sync_1_vvis), .Vis(sync_1_vis));
  LED led_1 (.in(sync_1_hsync_out));
  LED led_2 (.in(sync_1_vsync_out));
  LED led_3 (.in(sync_1_hvis));
  LED led_4 (.in(sync_1_vvis));
  LED led_5 (.in(sync_1_vis));
  Hex_Digit_Display hex_digit_display_1 (.value(HCOUNT_OUT[11:8]));  // open: dp
  Hex_Digit_Display hex_digit_display_2 (.value(HCOUNT_OUT[7:4]));  // open: dp
  Hex_Digit_Display hex_digit_display_3 (.value(VCOUNT_OUT[11:8]));  // open: dp
  Hex_Digit_Display hex_digit_display_4 (.value(VCOUNT_OUT[7:4]));  // open: dp
  Hex_Digit_Display hex_digit_display_5 (.value(HCOUNT_OUT[3:0]));  // open: dp
  Hex_Digit_Display hex_digit_display_6 (.value(VCOUNT_OUT[3:0]));  // open: dp

  // Notes on the sheet:
  //   Start hsync pulse at 31F
  //   End hsync pulse at 5F
  //   End of scanline at 8F
  //   Start vsync pulse at 1E9
  //   End vsync pulse at 1EB
  //   End of frame at 20C
endmodule

module HCount (
  input  CLK,
  input  nRST,
  output [11:0] HCOUNT_OUT,
  output BeginPulse,
  output EndPulse,
  output HSCAN_END,
  output HVisEnd
);

  wire n74163_1_pin1, n74163_1_pin3, n74163_1_pin7, n74163_1_pin15, n74163_2_pin15;

  _74163 #(.ShowInternalStructure("true")) u_74163_1 (
    .pin1(n74163_1_pin1), .pin2(CLK), .pin3(n74163_1_pin3), .pin4(n74163_1_pin3), .pin5(n74163_1_pin3),
    .pin6(n74163_1_pin3), .pin7(n74163_1_pin7), .pin15(n74163_1_pin15), .pin14(HCOUNT_OUT[0]),
    .pin13(HCOUNT_OUT[1]), .pin12(HCOUNT_OUT[2]), .pin11(HCOUNT_OUT[3]), .pin10(n74163_1_pin7),
    .pin9(n74163_1_pin7));
  _74163 #(.ShowInternalStructure("true")) u_74163_2 (
    .pin1(n74163_1_pin1), .pin2(CLK), .pin3(n74163_1_pin3), .pin4(n74163_1_pin3), .pin5(n74163_1_pin3),
    .pin6(n74163_1_pin3), .pin7(n74163_1_pin15), .pin15(n74163_2_pin15), .pin14(HCOUNT_OUT[4]),
    .pin13(HCOUNT_OUT[5]), .pin12(HCOUNT_OUT[6]), .pin11(HCOUNT_OUT[7]), .pin10(n74163_1_pin15),
    .pin9(n74163_1_pin7));
  _74163 #(.ShowInternalStructure("true")) u_74163_3 (
    .pin1(n74163_1_pin1), .pin2(CLK), .pin3(n74163_1_pin3), .pin4(n74163_1_pin3), .pin5(n74163_1_pin3),
    .pin6(n74163_1_pin3), .pin7(n74163_2_pin15), .pin14(HCOUNT_OUT[8]), .pin13(HCOUNT_OUT[9]),
    .pin12(HCOUNT_OUT[10]), .pin11(HCOUNT_OUT[11]), .pin10(n74163_2_pin15), .pin9(n74163_1_pin7));  // open: pin15
  HCntCtrl hcntctrl_1 (
    .HCOUNT(HCOUNT_OUT), .nRST(nRST), .BeginPulse(BeginPulse), .nHCCLR(n74163_1_pin1), .EndPulse(EndPulse),
    .HSCAN_END(HSCAN_END), .HVisEnd(HVisEnd));
  // also tied to GND on the sheet: n74163_1_pin3
  // also tied to VCC on the sheet: n74163_1_pin7

  // Notes on the sheet:
  //   Counters reset when nRST or BeginPulse asserted
endmodule

module VCount (
  input  CLK,
  input  nRST,
  input  HSCAN_END,
  output [11:0] VCOUNT_OUT,
  output VCOUNT_END,
  output BeginPulse,
  output EndPulse,
  output VVisEnd
);

  wire n74163_1_pin1, n74163_1_pin7, n74163_1_pin15, n74163_2_pin15, n74163_3_pin5;
  wire [9:0] n74163_1_pin3;

  _74163 #(.ShowInternalStructure("true")) u_74163_1 (
    .pin1(n74163_1_pin1), .pin2(CLK), .pin3(n74163_1_pin3[0]), .pin4(n74163_1_pin3[1]),
    .pin5(n74163_1_pin3[2]), .pin6(n74163_1_pin3[3]), .pin7(n74163_1_pin7), .pin15(n74163_1_pin15),
    .pin14(VCOUNT_OUT[0]), .pin13(VCOUNT_OUT[1]), .pin12(VCOUNT_OUT[2]), .pin11(VCOUNT_OUT[3]),
    .pin10(HSCAN_END), .pin9(nRST));
  _74163 #(.ShowInternalStructure("true")) u_74163_2 (
    .pin1(n74163_1_pin1), .pin2(CLK), .pin3(n74163_1_pin3[4]), .pin4(n74163_1_pin3[5]),
    .pin5(n74163_1_pin3[6]), .pin6(n74163_1_pin3[7]), .pin7(n74163_1_pin15), .pin15(n74163_2_pin15),
    .pin14(VCOUNT_OUT[4]), .pin13(VCOUNT_OUT[5]), .pin12(VCOUNT_OUT[6]), .pin11(VCOUNT_OUT[7]),
    .pin10(n74163_1_pin15), .pin9(nRST));
  VCntCtrl vcntctrl_1 (
    .VCOUNT(VCOUNT_OUT), .HSCAN_END(HSCAN_END), .VCOUNT_END(VCOUNT_END), .nVCCLR(n74163_1_pin1),
    .BeginPulse(BeginPulse), .EndPulse(EndPulse), .VVisEnd(VVisEnd));
  _74163 #(.ShowInternalStructure("true")) u_74163_3 (
    .pin1(n74163_1_pin1), .pin2(CLK), .pin3(n74163_1_pin3[8]), .pin4(n74163_1_pin3[9]), .pin5(n74163_3_pin5),
    .pin6(n74163_3_pin5), .pin7(n74163_2_pin15), .pin14(VCOUNT_OUT[8]), .pin13(VCOUNT_OUT[9]),
    .pin12(VCOUNT_OUT[10]), .pin11(VCOUNT_OUT[11]), .pin10(n74163_2_pin15), .pin9(nRST));  // open: pin15
  // also tied to GND on the sheet: {n74163_1_pin3[1], n74163_1_pin3[2], n74163_1_pin3[4], n74163_1_pin3[9], n74163_3_pin5}
  // also tied to VCC on the sheet: {n74163_1_pin3[0], n74163_1_pin3[3], n74163_1_pin3[5], n74163_1_pin3[6], n74163_1_pin3[7], n74163_1_pin3[8], n74163_1_pin7}

  // Notes on the sheet:
  //   Initial VCOUNT
endmodule

module HCntCtrl (
  input  [11:0] HCOUNT,
  input  nRST,
  output BeginPulse,
  output nHCCLR,
  output EndPulse,
  output HSCAN_END,
  output HVisEnd
);

  wire not_1_out, not_2_out, not_3_out, not_4_out, not_5_out, not_6_out, not_7_out, not_8_out, not_9_out,
       not_10_out, not_11_out, not_12_out, not_13_out, not_14_out, not_15_out, not_16_out, not_17_out,
       or_1_out;

  not not_1 (not_1_out, HCOUNT[5]);
  not not_2 (not_2_out, HCOUNT[5]);
  not not_3 (not_3_out, HCOUNT[4]);
  not not_4 (not_4_out, HCOUNT[8]);
  not not_5 (not_5_out, HCOUNT[4]);
  not not_6 (not_6_out, HCOUNT[6]);
  not not_7 (not_7_out, HCOUNT[7]);
  not not_8 (not_8_out, HCOUNT[8]);
  not not_9 (not_9_out, HCOUNT[5]);
  not not_10 (not_10_out, HCOUNT[6]);
  not not_11 (not_11_out, HCOUNT[9]);
  not not_12 (not_12_out, HCOUNT[5]);
  not not_13 (not_13_out, HCOUNT[6]);
  not not_14 (not_14_out, HCOUNT[7]);
  not not_15 (not_15_out, nRST);
  not not_16 (not_16_out, HCOUNT[9]);
  not not_17 (not_17_out, HCOUNT[7]);
  and and_1 (BeginPulse, HCOUNT[0], HCOUNT[1], HCOUNT[2], HCOUNT[3], HCOUNT[4], not_1_out, not_6_out, not_14_out, HCOUNT[8], HCOUNT[9]);
  or or_1 (or_1_out, not_15_out, BeginPulse);
  and and_2 (EndPulse, HCOUNT[0], HCOUNT[1], HCOUNT[2], HCOUNT[3], HCOUNT[4], not_2_out, HCOUNT[6], not_7_out, not_8_out, not_16_out);
  and and_3 (HSCAN_END, HCOUNT[0], HCOUNT[1], HCOUNT[2], HCOUNT[3], not_3_out, not_9_out, not_10_out, HCOUNT[7], not_4_out, not_11_out);
  and and_4 (HVisEnd, HCOUNT[0], HCOUNT[1], HCOUNT[2], HCOUNT[3], not_5_out, not_12_out, not_13_out, not_17_out, HCOUNT[8], HCOUNT[9]);
  not not_18 (nHCCLR, or_1_out);

  // Notes on the sheet:
  //   This circuit is intended to be equivalent to HCntCtrl.pld
  //   Counters cleared when nRST asserted or BeginPulse asserted
  //   HVisEnd asserted when HCOUNT=783 (binary 1100001111)
  //   BeginPulse asserted when HCOUNT=799 (binary 1100011111)
  //   EndPulse asserted when HCOUNT=95 (binary 0001011111)
  //   HSCAN_END asserted when HCOUNT=143 (binary 0010001111)
endmodule

module VCntCtrl (
  input  [11:0] VCOUNT,
  input  HSCAN_END,
  output VCOUNT_END,
  output nVCCLR,
  output BeginPulse,
  output EndPulse,
  output VVisEnd
);

  wire and_1_out, not_1_out, not_2_out, not_3_out, not_4_out, not_5_out, not_6_out, not_7_out, not_8_out,
       not_9_out, not_10_out, not_11_out, not_12_out, not_13_out;

  not not_1 (not_1_out, VCOUNT[0]);
  not not_2 (not_2_out, VCOUNT[1]);
  not not_3 (not_3_out, VCOUNT[4]);
  not not_4 (not_4_out, VCOUNT[5]);
  not not_5 (not_5_out, VCOUNT[1]);
  not not_6 (not_6_out, VCOUNT[2]);
  not not_7 (not_7_out, VCOUNT[2]);
  not not_8 (not_8_out, VCOUNT[5]);
  not not_9 (not_9_out, VCOUNT[6]);
  not not_10 (not_10_out, VCOUNT[7]);
  not not_11 (not_11_out, VCOUNT[4]);
  not not_12 (not_12_out, VCOUNT[4]);
  not not_13 (not_13_out, VCOUNT[8]);
  and and_1 (and_1_out, VCOUNT_END, HSCAN_END);
  and and_2 (VCOUNT_END, not_1_out, not_2_out, VCOUNT[2], VCOUNT[3], not_3_out, not_4_out, not_9_out, not_10_out, not_13_out, VCOUNT[9]);
  not not_14 (nVCCLR, and_1_out);
  and and_3 (BeginPulse, HSCAN_END, VCOUNT[0], not_5_out, not_6_out, VCOUNT[3], not_11_out, VCOUNT[5], VCOUNT[6], VCOUNT[7], VCOUNT[8]);
  and and_4 (EndPulse, HSCAN_END, VCOUNT[0], VCOUNT[1], not_7_out, VCOUNT[3], not_12_out, VCOUNT[5], VCOUNT[6], VCOUNT[7], VCOUNT[8]);
  and and_5 (VVisEnd, VCOUNT[0], VCOUNT[1], VCOUNT[2], VCOUNT[3], VCOUNT[4], not_8_out, VCOUNT[6], VCOUNT[7], VCOUNT[8]);

  // Notes on the sheet:
  //   This circuit is intended to be equivalent to VCntCtrl.pld
  //   Clear counters if (HSCAN_END & VCOUNT_END)
  //   VVisEnd generated when VCOUNT=479
  //   BeginPulse when HSCAN_END and VCOUNT=489
  //   EndPulse when HSCAN_END and VCOUNT=491
  //   VCOUNT_END when count is 524
endmodule

module Sync (
  input  CLK,
  input  nRST,
  input  HBeginPulse,
  input  HEndPulse,
  input  VBeginPulse,
  input  VEndPulse,
  input  HCOUNT_END,
  input  VCOUNT_END,
  input  HVisEnd,
  input  VVisEnd,
  output HSYNC_OUT,
  output VSYNC_OUT,
  output HVis,
  output VVis,
  output Vis
);

  wire and_1_out, and_2_out, and_3_out, and_4_out, and_5_out, and_6_out, and_7_out, not_1_out, not_2_out,
       not_3_out, not_4_out, not_5_out, not_6_out, not_7_out, not_8_out, or_1_out, or_2_out, or_3_out,
       or_4_out;

  not not_1 (not_1_out, HBeginPulse);
  not not_2 (not_2_out, VBeginPulse);
  not not_3 (not_3_out, VEndPulse);
  not not_4 (not_4_out, nRST);
  not not_5 (not_5_out, VVisEnd);
  not not_6 (not_6_out, HCOUNT_END);
  not not_7 (not_7_out, HVisEnd);
  and and_1 (and_1_out, HCOUNT_END, VCOUNT_END);
  and and_2 (and_2_out, not_5_out, VVis);
  and and_3 (and_3_out, VVisEnd, not_6_out, VVis);
  and and_4 (and_4_out, nRST, HEndPulse);
  and and_5 (and_5_out, nRST, not_1_out, HSYNC_OUT);
  and and_6 (and_6_out, not_2_out, not_3_out, VSYNC_OUT);
  and and_7 (and_7_out, not_7_out, HVis);
  or or_1 (or_1_out, and_4_out, and_5_out);
  or or_2 (or_2_out, not_8_out, VEndPulse, and_6_out);
  D_Flip_Flop d_ff_1 (.D(or_3_out), .clk(CLK), .Q(HVis), .preset(1'b0), .reset(1'b0));  // open: Qn
  or or_3 (or_3_out, not_4_out, HCOUNT_END, and_7_out);
  D_Flip_Flop d_ff_2 (.D(or_4_out), .clk(CLK), .Q(VVis), .preset(1'b0), .reset(1'b0));  // open: Qn
  or or_4 (or_4_out, and_1_out, and_2_out, and_3_out);
  D_Flip_Flop d_ff_3 (.D(or_1_out), .clk(CLK), .Q(HSYNC_OUT), .preset(1'b0), .reset(1'b0));  // open: Qn
  not not_8 (not_8_out, nRST);
  D_Flip_Flop d_ff_4 (.D(or_2_out), .clk(CLK), .Q(VSYNC_OUT), .preset(1'b0), .reset(1'b0));  // open: Qn
  and and_8 (Vis, HVis, VVis);

  // Notes on the sheet:
  //   This circuit is intended to be equivalent to Sync.pld
  //   VVis is initially false
  //    (VCOUNT starts in back porch)
endmodule

module Readout (
);

  _74163 u_74163_1 ();  // open: pin1, pin2, pin3, pin4, pin5, pin6, pin7, pin15, pin14, pin13, pin12, pin11, pin10, pin9
  _74163 u_74163_2 ();  // open: pin1, pin2, pin3, pin4, pin5, pin6, pin7, pin15, pin14, pin13, pin12, pin11, pin10, pin9
  _74163 u_74163_3 ();  // open: pin1, pin2, pin3, pin4, pin5, pin6, pin7, pin15, pin14, pin13, pin12, pin11, pin10, pin9
endmodule
