// Logisim project hw_vga_sim.circ as structural Verilog: 4 circuits, main circuit main
module main (
  input  nRST
);

  wire CLK_out, hcount_1_hcount_end, vcount_1_vcount_end;
  wire [11:0] hcount_1_hcount_out, vcount_1_vcount_out;

  Clock CLK (.out(CLK_out));
  HCount hcount_1 (
    .CLK(CLK_out), .nRST(nRST), .HCOUNT_OUT(hcount_1_hcount_out), .HCOUNT_END(hcount_1_hcount_end));  // open: nHCOUNT_END
  VCount vcount_1 (
    .CLK(CLK_out), .nRST(nRST), .HCOUNT_END(hcount_1_hcount_end), .VCOUNT_OUT(vcount_1_vcount_out),
    .VCOUNT_END(vcount_1_vcount_end));  // open: nVCOUNT_END
  Hex_Digit_Display hex_digit_display_1 (.value(hcount_1_hcount_out[11:8]));  // open: dp
  Hex_Digit_Display hex_digit_display_2 (.value(hcount_1_hcount_out[7:4]));  // open: dp
  Hex_Digit_Display hex_digit_display_3 (.value(vcount_1_vcount_out[11:8]));  // open: dp
  Hex_Digit_Display hex_digit_display_4 (.value(vcount_1_vcount_out[7:4]));  // open: dp
  LED led_1 (.in(vcount_1_vcount_end));
  Hex_Digit_Display hex_digit_display_5 (.value(hcount_1_hcount_out[3:0]));  // open: dp
  Hex_Digit_Display hex_digit_display_6 (.value(vcount_1_vcount_out[3:0]));  // open: dp
endmodule

module HCount (
  input  CLK,
  input  nRST,
  output [11:0] HCOUNT_OUT,
  output nHCOUNT_END,
  output HCOUNT_END
);

  wire n7411_1_pin1, n7411_1_pin3, n74163_1_pin1, n74163_1_pin3, n74163_1_pin7, n74163_1_pin15,
       n74163_2_pin15;
  wire [0:0] n7411_1_pin8;

  _74163 #(.ShowInternalStructure("true")) u_74163_1 (
    .pin1(n74163_1_pin1), .pin2(CLK), .pin3(n74163_1_pin3), .pin4(n74163_1_pin3), .pin5(n74163_1_pin3),
    .pin6(n74163_1_pin3), .pin7(n74163_1_pin7), .pin15(n74163_1_pin15), .pin14(HCOUNT_OUT[0]),
    .pin13(HCOUNT_OUT[1]), .pin12(HCOUNT_OUT[2]), .pin11(HCOUNT_OUT[3]), .pin10(n74163_1_pin7),
    .pin9(n74163_1_pin7));
  _7411 #(.ShowInternalStructure("true")) u_7411_1 (
    .pin1(n7411_1_pin1), .pin2(nHCOUNT_END), .pin3(n7411_1_pin3), .pin4(n7411_1_pin3), .pin5(n7411_1_pin3),
    .pin13(nRST), .pin12(n74163_1_pin1), .pin11(HCOUNT_OUT[0]), .pin10(HCOUNT_OUT[1]), .pin9(HCOUNT_OUT[2]),
    .pin8(n7411_1_pin8[0]));  // open: pin6
  _74163 #(.ShowInternalStructure("true")) u_74163_2 (
    .pin1(n74163_1_pin1), .pin2(CLK), .pin3(n74163_1_pin3), .pin4(n74163_1_pin3), .pin5(n74163_1_pin3),
    .pin6(n74163_1_pin3), .pin7(n74163_1_pin15), .pin15(n74163_2_pin15), .pin14(HCOUNT_OUT[4]),
    .pin13(HCOUNT_OUT[5]), .pin12(HCOUNT_OUT[6]), .pin11(HCOUNT_OUT[7]), .pin10(n74163_1_pin15),
    .pin9(n74163_1_pin7));
  _74163 #(.ShowInternalStructure("true")) u_74163_3 (
    .pin1(n74163_1_pin1), .pin2(CLK), .pin3(n74163_1_pin3), .pin4(n74163_1_pin3), .pin5(n74163_1_pin3),
    .pin6(n74163_1_pin3), .pin7(n74163_2_pin15), .pin14(HCOUNT_OUT[8]), .pin13(HCOUNT_OUT[9]),
    .pin12(HCOUNT_OUT[10]), .pin11(HCOUNT_OUT[11]), .pin10(n74163_2_pin15), .pin9(n74163_1_pin7));  // open: pin15
  not not_1 (nHCOUNT_END, HCOUNT_END);
  Comparator #(.mode("unsigned")) comparator_1 (
    .a({HCOUNT_OUT[9:3], n7411_1_pin8[0]}), .b(8'hc7), .eq(HCOUNT_END));  // open: gt, lt
  // also tied to GND on the sheet: {n7411_1_pin3, n74163_1_pin3}
  // also tied to VCC on the sheet: {n74163_1_pin7, n7411_1_pin1}

  // Notes on the sheet:
  //   Counters reset when nRST or nHCOUNT_END asserted
  //   HCOUNT_END when HCOUNT is 799
endmodule

module VCount (
  input  CLK,
  input  nRST,
  input  HCOUNT_END,
  output [11:0] VCOUNT_OUT,
  output nVCOUNT_END,
  output VCOUNT_END
);

  wire n7411_1_pin1, n7411_1_pin2, n7411_1_pin6, n74163_1_pin1, n74163_1_pin3, n74163_1_pin7, n74163_1_pin9,
       n74163_1_pin15, n74163_2_pin15;
  wire [0:0] n7411_1_pin8;

  _74163 #(.ShowInternalStructure("true")) u_74163_1 (
    .pin1(n74163_1_pin1), .pin2(CLK), .pin3(n74163_1_pin3), .pin4(n74163_1_pin3), .pin5(n74163_1_pin3),
    .pin6(n74163_1_pin3), .pin7(n74163_1_pin7), .pin15(n74163_1_pin15), .pin14(VCOUNT_OUT[0]),
    .pin13(VCOUNT_OUT[1]), .pin12(VCOUNT_OUT[2]), .pin11(VCOUNT_OUT[3]), .pin10(HCOUNT_END),
    .pin9(n74163_1_pin9));
  _74163 #(.ShowInternalStructure("true")) u_74163_2 (
    .pin1(n74163_1_pin1), .pin2(CLK), .pin3(n74163_1_pin3), .pin4(n74163_1_pin3), .pin5(n74163_1_pin3),
    .pin6(n74163_1_pin3), .pin7(n74163_1_pin15), .pin15(n74163_2_pin15), .pin14(VCOUNT_OUT[4]),
    .pin13(VCOUNT_OUT[5]), .pin12(VCOUNT_OUT[6]), .pin11(VCOUNT_OUT[7]), .pin10(n74163_1_pin15),
    .pin9(n74163_1_pin9));
  _7411 #(.ShowInternalStructure("true")) u_7411_1 (
    .pin1(n7411_1_pin1), .pin2(n7411_1_pin2), .pin3(VCOUNT_END), .pin4(HCOUNT_END), .pin5(n7411_1_pin1),
    .pin6(n7411_1_pin6), .pin13(nRST), .pin12(n74163_1_pin1), .pin11(VCOUNT_OUT[2]), .pin10(VCOUNT_OUT[3]),
    .pin9(VCOUNT_OUT[9]), .pin8(n7411_1_pin8[0]));
  not not_1 (n7411_1_pin2, n7411_1_pin6);
  _74163 #(.ShowInternalStructure("true")) u_74163_3 (
    .pin1(n74163_1_pin1), .pin2(CLK), .pin3(n74163_1_pin3), .pin4(n74163_1_pin3), .pin5(n74163_1_pin3),
    .pin6(n74163_1_pin3), .pin7(n74163_2_pin15), .pin14(VCOUNT_OUT[8]), .pin13(VCOUNT_OUT[9]),
    .pin12(VCOUNT_OUT[10]), .pin11(VCOUNT_OUT[11]), .pin10(n74163_2_pin15), .pin9(n74163_1_pin9));  // open: pin15
  not not_2 (nVCOUNT_END, VCOUNT_END);
  Comparator #(.mode("unsigned")) comparator_1 (
    .a({VCOUNT_OUT[8:4], VCOUNT_OUT[1:0], n7411_1_pin8[0]}), .b(8'h1), .eq(VCOUNT_END));  // open: gt, lt
  // also tied to GND on the sheet: n74163_1_pin3
  // also tied to VCC on the sheet: {n74163_1_pin7, n74163_1_pin9, n7411_1_pin1}

  // Notes on the sheet:
  //   Counters reset if nRST asserted or both VCOUNT_END and HCOUNT_END asserted
  //   VCOUNT_END when count is 524
endmodule

module Sync (
  input  CLK,
  input  nRST,
  input  [11:0] HCOUNT
);

  wire n7474_1_pin1;

  _74157 #(.ShowInternalStructure("true")) u_74157_1 ();  // open: pin1, pin2, pin3, pin4, pin5, pin6, pin7, pin15, pin14, pin13, pin12, pin11, pin10, pin9
  _7474 #(.ShowInternalStructure("true")) u_7474_1 (
    .pin1(n7474_1_pin1), .pin3(CLK), .pin4(nRST));  // open: pin2, pin5, pin6, pin13, pin12, pin11, pin10, pin9, pin8
  // also tied to VCC on the sheet: n7474_1_pin1
endmodule
